# Fritzing sketch particle-dht11-sensor (saved by Fritzing 0.9.3b)

parts:
  Part1 = Photon
  Sunfounder1 = Humidity Sensor DHT11 [package=THT]

nets:
  N1: Part1.D4, Sunfounder1.Vout
  GND: Part1.GND, Sunfounder1.GND
  3V3: Part1.3V3, Sunfounder1.Vcc

custom parts:
  Humidity Sensor DHT11: Humidity Sensor DHT11 for Sunfounder 37 Sensor Kit
